// Logisim project logism_procs.circ as structural Verilog
module \bit  (
  input  in_1,
  input  in_2,
  output out_3
);

  wire nor_2_out;

  nor nor_1 (out_3, in_2, nor_2_out);
  nor nor_2 (nor_2_out, out_3, in_1);
endmodule

module _8b (
  input  in_1,
  input  in_2,
  input  in_3,
  input  in_4,
  input  in_5,
  input  in_6,
  input  in_7,
  input  in_8,
  input  in_9,
  input  in_10,
  input  in_11,
  output out_12,
  output out_13,
  output out_14,
  output out_15,
  output out_16,
  output out_17,
  output out_18,
  output out_19
);

  wire and_1_out, and_2_out, and_3_out, and_4_out, and_5_out, and_6_out, and_7_out, and_8_out, bit_1_out_3,
       bit_2_out_3, bit_3_out_3, bit_4_out_3, bit_5_out_3, bit_6_out_3, bit_7_out_3, bit_8_out_3, or_1_out;

  and and_1 (and_1_out, in_2, in_4);
  and and_2 (and_2_out, in_2, in_5);
  and and_3 (and_3_out, in_2, in_6);
  and and_4 (and_4_out, in_2, in_7);
  and and_5 (and_5_out, in_2, in_8);
  and and_6 (and_6_out, in_2, in_9);
  and and_7 (and_7_out, in_2, in_10);
  and and_8 (and_8_out, in_2, in_11);
  or or_1 (or_1_out, in_1, in_3);
  \bit  bit_1 (.in_1(and_1_out), .in_2(or_1_out), .out_3(bit_1_out_3));
  \bit  bit_2 (.in_1(and_2_out), .in_2(or_1_out), .out_3(bit_2_out_3));
  \bit  bit_3 (.in_1(and_3_out), .in_2(or_1_out), .out_3(bit_3_out_3));
  \bit  bit_4 (.in_1(and_4_out), .in_2(or_1_out), .out_3(bit_4_out_3));
  \bit  bit_5 (.in_1(and_5_out), .in_2(or_1_out), .out_3(bit_5_out_3));
  \bit  bit_6 (.in_1(and_6_out), .in_2(or_1_out), .out_3(bit_6_out_3));
  \bit  bit_7 (.in_1(and_7_out), .in_2(or_1_out), .out_3(bit_7_out_3));
  \bit  bit_8 (.in_1(and_8_out), .in_2(or_1_out), .out_3(bit_8_out_3));
  and and_9 (out_12, in_2, bit_1_out_3);
  and and_10 (out_13, in_2, bit_2_out_3);
  and and_11 (out_14, in_2, bit_3_out_3);
  and and_12 (out_15, in_2, bit_4_out_3);
  and and_13 (out_16, in_2, bit_5_out_3);
  and and_14 (out_17, in_2, bit_6_out_3);
  and and_15 (out_18, in_2, bit_7_out_3);
  and and_16 (out_19, in_2, bit_8_out_3);
endmodule

module _8B (
  input  in_1,
  input  in_2,
  input  in_3,
  input  in_4,
  input  in_5,
  input  in_6,
  input  in_7,
  input  in_8
);
endmodule
